// Logisim project R-I-S_Type_datapath.circ as structural Verilog: 3 circuits, main circuit main
module main (
  output [6:0] out_1
);

  wire clock_1_out, comparator_1_eq, comparator_2_eq, comparator_3_eq, comparator_4_gt, comparator_5_eq,
       Restart_Program_out;
  wire [31:0] adder_1_out, alu_1_output, bit_extender_1_out, multiplexer_1_out, reg_file_1_read_data_1,
       reg_file_1_read_data_2, register_1_q;
  wire [31:7] rom_1_data;

  Register #(.width(32)) register_1 (
    .D(adder_1_out), .Q(register_1_q), .clk(clock_1_out), .clr(Restart_Program_out));  // open: en
  Clock clock_1 (.out(clock_1_out));
  Button Restart_Program (.out(Restart_Program_out));
  Adder #(.width(32)) adder_1 (.a(32'h4), .b(register_1_q), .out(adder_1_out));  // open: cin, cout
  ROM #(.addrWidth(23), .dataWidth(32)) rom_1 (.addr(register_1_q[24:2]), .data({rom_1_data, out_1}));  // open: sel
  Comparator #(.width(7), .mode("unsigned")) comparator_1 (
    .a(out_1), .b(7'b0010011), .eq(comparator_1_eq));  // open: gt, lt
  assign bit_extender_1_out = {{20{rom_1_data[31]}}, rom_1_data[31:20]};  // Bit_Extender bit_extender_1
  Comparator #(.width(7), .mode("unsigned")) comparator_2 (
    .a(out_1), .b(7'b0000011), .eq(comparator_2_eq));  // open: gt, lt
  reg_file reg_file_1 (
    .reg_enb(1'b1), .Write_Data(alu_1_output), .Write_Register(rom_1_data[11:7]),
    .Read_Register_1(rom_1_data[19:15]), .Read_Register_2(rom_1_data[24:20]), .clk(clock_1_out),
    .Read_Data_1(reg_file_1_read_data_1), .Read_Data_2(reg_file_1_read_data_2));
  Comparator #(.width(7), .mode("unsigned")) comparator_3 (
    .a(out_1), .b(7'b0110011), .eq(comparator_3_eq));  // open: gt, lt
  Comparator #(.width(1)) comparator_4 (
    .a(comparator_1_eq), .b(comparator_3_eq), .gt(comparator_4_gt));  // open: eq, lt
  Multiplexer #(.width(32), .enable("false")) multiplexer_1 (
    .in0(bit_extender_1_out), .in1(reg_file_1_read_data_2), .out(multiplexer_1_out), .sel(comparator_4_gt));
  Comparator #(.width(7), .mode("unsigned")) comparator_5 (
    .a(out_1), .b(7'b0100011), .eq(comparator_5_eq));  // open: gt, lt
  ALU alu_1 (
    .INPUT_1(reg_file_1_read_data_1), .INPUT_2(multiplexer_1_out), .SRA_SRL(rom_1_data[30]),
    .OUTPUT(alu_1_output), .add_sub(rom_1_data[30]), .FUNC_3(rom_1_data[14:12]));  // open: Carry_In_add, Carry_In_sub, Carry_out_add, Carry_out_sub
  RAM #(.addrWidth(23), .dataWidth(32), .bus("separate")) ram_1 (
    .addr(alu_1_output[24:2]), .din(reg_file_1_read_data_2), .data(alu_1_output), .str(comparator_5_eq),
    .clk(clock_1_out), .ld(comparator_2_eq));  // open: sel, clr

  // Notes on the sheet:
  //   contents of rom_1 (hex, n*v repeats v):
  //   2303 7002b3 140413 6283b3
endmodule

// REG_F
module reg_file (
  input  reg_enb,
  input  clk,
  input  [31:0] Write_Data,
  input  [4:0] Write_Register,
  input  [4:0] Read_Register_1,
  input  [4:0] Read_Register_2,
  output [31:0] Read_Data_1,
  output [31:0] Read_Data_2
);

  wire [31:0] demultiplexer_1_out1, demultiplexer_1_out2, demultiplexer_1_out3, demultiplexer_1_out4,
       demultiplexer_1_out5, demultiplexer_1_out6, demultiplexer_1_out7, demultiplexer_1_out8,
       demultiplexer_1_out9, demultiplexer_1_out10, demultiplexer_1_out11, demultiplexer_1_out12,
       demultiplexer_1_out13, demultiplexer_1_out14, demultiplexer_1_out15, demultiplexer_1_out16,
       demultiplexer_1_out17, demultiplexer_1_out18, demultiplexer_1_out19, demultiplexer_1_out20,
       demultiplexer_1_out21, demultiplexer_1_out22, demultiplexer_1_out23, demultiplexer_1_out24,
       demultiplexer_1_out25, demultiplexer_1_out26, demultiplexer_1_out27, demultiplexer_1_out28,
       demultiplexer_1_out29, demultiplexer_1_out30, demultiplexer_1_out31, register_1_q, register_2_q,
       register_3_q, register_4_q, register_5_q, register_6_q, register_7_q, register_8_q, register_9_q,
       register_10_q, register_11_q, register_12_q, register_13_q, register_14_q, register_15_q,
       register_16_q, register_17_q, register_18_q, register_19_q, register_20_q, register_21_q,
       register_22_q, register_23_q, register_24_q, register_25_q, register_26_q, register_27_q,
       register_28_q, register_29_q, register_30_q, register_31_q;

  // Probe on Write_Register
  Demultiplexer #(.select(5), .width(32), .enable("false")) demultiplexer_1 (
    .out1(demultiplexer_1_out1), .out2(demultiplexer_1_out2), .out3(demultiplexer_1_out3),
    .out4(demultiplexer_1_out4), .out5(demultiplexer_1_out5), .out6(demultiplexer_1_out6),
    .out7(demultiplexer_1_out7), .out8(demultiplexer_1_out8), .out9(demultiplexer_1_out9),
    .out10(demultiplexer_1_out10), .out11(demultiplexer_1_out11), .out12(demultiplexer_1_out12),
    .out13(demultiplexer_1_out13), .out14(demultiplexer_1_out14), .out15(demultiplexer_1_out15),
    .out16(demultiplexer_1_out16), .out17(demultiplexer_1_out17), .out18(demultiplexer_1_out18),
    .out19(demultiplexer_1_out19), .out20(demultiplexer_1_out20), .out21(demultiplexer_1_out21),
    .out22(demultiplexer_1_out22), .out23(demultiplexer_1_out23), .out24(demultiplexer_1_out24),
    .out25(demultiplexer_1_out25), .out26(demultiplexer_1_out26), .out27(demultiplexer_1_out27),
    .out28(demultiplexer_1_out28), .out29(demultiplexer_1_out29), .out30(demultiplexer_1_out30),
    .out31(demultiplexer_1_out31), .in(Write_Data), .sel(Write_Register));  // open: out0
  Register #(.width(32)) register_1 (.D(demultiplexer_1_out1), .en(reg_enb), .Q(register_1_q), .clk(clk));  // open: clr
  Register #(.width(32)) register_2 (.D(demultiplexer_1_out2), .en(reg_enb), .Q(register_2_q), .clk(clk));  // open: clr
  Register #(.width(32)) register_3 (.D(demultiplexer_1_out3), .en(reg_enb), .Q(register_3_q), .clk(clk));  // open: clr
  Register #(.width(32)) register_4 (.D(demultiplexer_1_out4), .en(reg_enb), .Q(register_4_q), .clk(clk));  // open: clr
  Register #(.width(32)) register_5 (.D(demultiplexer_1_out5), .en(reg_enb), .Q(register_5_q), .clk(clk));  // open: clr
  Register #(.width(32)) register_6 (.D(demultiplexer_1_out6), .en(reg_enb), .Q(register_6_q), .clk(clk));  // open: clr
  Register #(.width(32)) register_7 (.D(demultiplexer_1_out7), .en(reg_enb), .Q(register_7_q), .clk(clk));  // open: clr
  Register #(.width(32)) register_8 (.D(demultiplexer_1_out8), .en(reg_enb), .Q(register_8_q), .clk(clk));  // open: clr
  Register #(.width(32)) register_9 (.D(demultiplexer_1_out9), .en(reg_enb), .Q(register_9_q), .clk(clk));  // open: clr
  Register #(.width(32)) register_10 (
    .D(demultiplexer_1_out10), .en(reg_enb), .Q(register_10_q), .clk(clk));  // open: clr
  Register #(.width(32)) register_11 (
    .D(demultiplexer_1_out11), .en(reg_enb), .Q(register_11_q), .clk(clk));  // open: clr
  Register #(.width(32)) register_12 (
    .D(demultiplexer_1_out12), .en(reg_enb), .Q(register_12_q), .clk(clk));  // open: clr
  Register #(.width(32)) register_13 (
    .D(demultiplexer_1_out13), .en(reg_enb), .Q(register_13_q), .clk(clk));  // open: clr
  Register #(.width(32)) register_14 (
    .D(demultiplexer_1_out14), .en(reg_enb), .Q(register_14_q), .clk(clk));  // open: clr
  Register #(.width(32)) register_15 (
    .D(demultiplexer_1_out15), .en(reg_enb), .Q(register_15_q), .clk(clk));  // open: clr
  Register #(.width(32)) register_16 (
    .D(demultiplexer_1_out16), .en(reg_enb), .Q(register_16_q), .clk(clk));  // open: clr
  Register #(.width(32)) register_17 (
    .D(demultiplexer_1_out17), .en(reg_enb), .Q(register_17_q), .clk(clk));  // open: clr
  Register #(.width(32)) register_18 (
    .D(demultiplexer_1_out18), .en(reg_enb), .Q(register_18_q), .clk(clk));  // open: clr
  Register #(.width(32)) register_19 (
    .D(demultiplexer_1_out19), .en(reg_enb), .Q(register_19_q), .clk(clk));  // open: clr
  Register #(.width(32)) register_20 (
    .D(demultiplexer_1_out20), .en(reg_enb), .Q(register_20_q), .clk(clk));  // open: clr
  Register #(.width(32)) register_21 (
    .D(demultiplexer_1_out21), .en(reg_enb), .Q(register_21_q), .clk(clk));  // open: clr
  Register #(.width(32)) register_22 (
    .D(demultiplexer_1_out22), .en(reg_enb), .Q(register_22_q), .clk(clk));  // open: clr
  Register #(.width(32)) register_23 (
    .D(demultiplexer_1_out23), .en(reg_enb), .Q(register_23_q), .clk(clk));  // open: clr
  Register #(.width(32)) register_24 (
    .D(demultiplexer_1_out24), .en(reg_enb), .Q(register_24_q), .clk(clk));  // open: clr
  Register #(.width(32)) register_25 (
    .D(demultiplexer_1_out25), .en(reg_enb), .Q(register_25_q), .clk(clk));  // open: clr
  Register #(.width(32)) register_26 (
    .D(demultiplexer_1_out26), .en(reg_enb), .Q(register_26_q), .clk(clk));  // open: clr
  Register #(.width(32)) register_27 (
    .D(demultiplexer_1_out27), .en(reg_enb), .Q(register_27_q), .clk(clk));  // open: clr
  Register #(.width(32)) register_28 (
    .D(demultiplexer_1_out28), .en(reg_enb), .Q(register_28_q), .clk(clk));  // open: clr
  Register #(.width(32)) register_29 (.D(demultiplexer_1_out29), .en(reg_enb), .Q(register_29_q), .clk(clk), .clr(clk));
  Register #(.width(32)) register_30 (
    .D(demultiplexer_1_out30), .en(reg_enb), .Q(register_30_q), .clk(clk));  // open: clr
  Register #(.width(32)) register_31 (
    .D(demultiplexer_1_out31), .en(reg_enb), .Q(register_31_q), .clk(clk));  // open: clr
  Multiplexer #(.select(5), .width(32), .enable("false")) multiplexer_1 (
    .in0({32{1'b0}}), .in1(register_1_q), .in2(register_2_q), .in3(register_3_q), .in4(register_4_q),
    .in5(register_5_q), .in6(register_6_q), .in7(register_7_q), .in8(register_8_q), .in9(register_9_q),
    .in10(register_10_q), .in11(register_11_q), .in12(register_12_q), .in13(register_13_q),
    .in14(register_14_q), .in15(register_15_q), .in16(register_16_q), .in17(register_17_q),
    .in18(register_18_q), .in19(register_19_q), .in20(register_20_q), .in21(register_21_q),
    .in22(register_22_q), .in23(register_23_q), .in24(register_24_q), .in25(register_25_q),
    .in26(register_26_q), .in27(register_27_q), .in28(register_28_q), .in29(register_29_q),
    .in30(register_30_q), .in31(register_31_q), .out(Read_Data_1), .sel(Read_Register_1));
  // Probe on Read_Register_1
  Multiplexer #(.select(5), .width(32), .enable("false")) multiplexer_2 (
    .in0({32{1'b0}}), .in1(register_1_q), .in2(register_2_q), .in3(register_3_q), .in4(register_4_q),
    .in5(register_5_q), .in6(register_6_q), .in7(register_7_q), .in8(register_8_q), .in9(register_9_q),
    .in10(register_10_q), .in11(register_11_q), .in12(register_12_q), .in13(register_13_q),
    .in14(register_14_q), .in15(register_15_q), .in16(register_16_q), .in17(register_17_q),
    .in18(register_18_q), .in19(register_19_q), .in20(register_20_q), .in21(register_21_q),
    .in22(register_22_q), .in23(register_23_q), .in24(register_24_q), .in25(register_25_q),
    .in26(register_26_q), .in27(register_27_q), .in28(register_28_q), .in29(register_29_q),
    .in30(register_30_q), .in31(register_31_q), .out(Read_Data_2), .sel(Read_Register_2));
  // Probe on Read_Register_2
endmodule

module ALU (
  input  [31:0] INPUT_1,
  input  [31:0] INPUT_2,
  input  Carry_In_add,
  input  Carry_In_sub,
  input  add_sub,
  input  SRA_SRL,
  input  [2:0] FUNC_3,
  output Carry_out_add,
  output Carry_out_sub,
  output [31:0] OUTPUT
);

  wire comparator_1_eq, comparator_1_gt, comparator_1_lt, comparator_2_eq, comparator_2_gt, comparator_2_lt;
  wire [31:0] adder_1_out, and_1_out, multiplexer_1_out, multiplexer_3_out, or_1_out, shifter_1_out,
       shifter_2_out, shifter_3_out, subtractor_1_out, undriven, undriven_2, xor_1_out;

  Comparator #(.width(32)) comparator_1 (
    .a(INPUT_1), .b(INPUT_2), .gt(comparator_1_gt), .eq(comparator_1_eq), .lt(comparator_1_lt));
  Comparator #(.width(32), .mode("unsigned")) comparator_2 (
    .a(INPUT_1), .b(INPUT_2), .gt(comparator_2_gt), .eq(comparator_2_eq), .lt(comparator_2_lt));
  Adder #(.width(32)) adder_1 (.a(INPUT_1), .b(INPUT_2), .out(adder_1_out), .cin(Carry_In_add), .cout(Carry_out_add));
  Subtractor #(.width(32)) subtractor_1 (
    .a(INPUT_1), .b(INPUT_2), .out(subtractor_1_out), .bin(Carry_In_sub), .bout(Carry_out_sub));
  Multiplexer #(.width(32), .enable("false")) multiplexer_1 (
    .in0(adder_1_out), .in1(subtractor_1_out), .out(multiplexer_1_out), .sel(add_sub));
  assign and_1_out = INPUT_1 & INPUT_2;  // AND_Gate and_1, 32 bits wide
  assign or_1_out = INPUT_1 | INPUT_2;  // OR_Gate or_1, 32 bits wide
  assign xor_1_out = INPUT_1 ^ INPUT_2;  // XOR_Gate xor_1, 32 bits wide
  Multiplexer #(.select(3), .width(32), .enable("false")) multiplexer_2 (
    .in0(multiplexer_1_out), .in1(shifter_3_out), .in2(undriven), .in3(undriven_2), .in4(xor_1_out),
    .in5(multiplexer_3_out), .in6(or_1_out), .in7(and_1_out), .out(OUTPUT), .sel(FUNC_3));
  Shifter #(.width(32), .shift("ar")) shifter_1 (.in(INPUT_1), .\dist (INPUT_2[4:0]), .out(shifter_1_out));
  Shifter #(.width(32), .shift("lr")) shifter_2 (.in(INPUT_1), .\dist (INPUT_2[4:0]), .out(shifter_2_out));
  Multiplexer #(.width(32), .enable("false")) multiplexer_3 (
    .in0(shifter_2_out), .in1(shifter_1_out), .out(multiplexer_3_out), .sel(SRA_SRL));
  Shifter #(.width(32)) shifter_3 (.in(INPUT_1), .\dist (INPUT_2[4:0]), .out(shifter_3_out));

  // Notes on the sheet:
  //   SLT
  //   SLT-U
  //   ADD
  //   SUB
  //   AND
  //   OR
  //   XOR
  //   SRA
  //   SRL
  //   SLL
endmodule
